# Fritzing sketch ESP8266-MQTT-Sensor (saved by Fritzing 0.8.5b)
breadboards: 1

parts:
  WeMos_D1_Mini1 = WeMos D1 Mini
  R1 = Resistor [tolerance=±5% resistance=4.7k package=THT]
  DHT2 = DHT22 Humidity and Temperature Sensor
  R2 = Resistor [tolerance=±5% resistance=4.7k package=THT]
  DHT3 = DHT22 Humidity and Temperature Sensor
  DHT1 = DHT22 Humidity and Temperature Sensor
  R3 = Resistor [tolerance=±5% resistance=4.7k package=THT]

nets:
  VDD: WeMos_D1_Mini1.3V3, R1.Pin_1, DHT2.VDD, R2.Pin_1, DHT3.VDD, DHT1.VDD, R3.Pin_1
  N1: WeMos_D1_Mini1.D2, DHT3.DATA, R3.Pin_0
  N2: WeMos_D1_Mini1.D3, DHT2.DATA, R2.Pin_0
  N3: WeMos_D1_Mini1.D4, R1.Pin_0, DHT1.DATA
  GND: WeMos_D1_Mini1.G, DHT2.GND, DHT3.GND, DHT1.GND

custom parts:
  WeMos D1 Mini: The D1 mini is a mini wifi board based on ESP-8266EX.
